# Fritzing sketch 33-HandScanner (saved by Fritzing 1.0.6)
breadboards: 1

parts:
  Ledstrip_Rechts = SMD RGB LED (WS2812) [package=5050]
  knop = Square Pushbutton
  R9 = Resistor [tolerance=±5% resistance=470 package="0603 [SMD]"]
  1000uF_25V = Capacitor Polarized [package=panasonic_g]
  R13 = Resistor [tolerance=±5% resistance=470k package="0603 [SMD]"]
  Nano = Arduino Micro (Rev3)
  Ledstrip_Links = SMD RGB LED (WS2812) [package=5050]
  R14 = Resistor [tolerance=±5% resistance=470 package="0603 [SMD]"]
  Ledstrip_BOVEN = SMD RGB LED (WS2812) [package=5050]
  R15 = Resistor [tolerance=±5% resistance=470 package="0603 [SMD]"]
  Ledstrip_Onder = SMD RGB LED (WS2812) [package=5050]
  R16 = Resistor [tolerance=±5% resistance=470 package="0603 [SMD]"]
  1000uF_25V1 = Capacitor Polarized [package=panasonic_g]  # not connected
  1000uF_25V2 = Capacitor Polarized [package=panasonic_g]  # not connected
  1000uF_25V3 = Capacitor Polarized [package=panasonic_g]  # not connected

nets:
  N1: Ledstrip_Rechts.DIn, R9.Pin_1
  5V: Ledstrip_Rechts.VCC, 1000uF_25V.+, Nano.5V
  N2: knop.leg0, Nano.D2/SDA
  GND: knop.leg1, Nano.GND
  N3: R9.Pin_0, Nano.A0, R14.Pin_0
  N4: R13.Pin_0, Nano.D4_PWM/A6
  N5: R13.Pin_1, Nano.D6_PWM/A7
  N6: Nano.A2, R15.Pin_0
  N7: Nano.A1, R16.Pin_0
  N8: Ledstrip_Links.DIn, R14.Pin_1
  N9: Ledstrip_BOVEN.DIn, R15.Pin_1
  N10: Ledstrip_Onder.DIn, R16.Pin_1

notes:
  Spiegel
  TouchPlaat
  Zwart
  Geel
  Oranje
  Bruin
  Blauw
