# Fritzing sketch 47a-KikkerkokenInput (saved by Fritzing 1.0.6)
circuit board: 8.46667cm x 5.64444cm
breadboards: 1

parts:
  Lestrip_warmwit = SMD RGB LED (WS2812) [package=5050]
  Ledstrip_RGB = SMD RGB LED (WS2812) [package=5050]
  4a = Square Pushbutton
  3b = Square Pushbutton
  3a = Square Pushbutton
  2b = Square Pushbutton
  2a = Square Pushbutton
  1b = Square Pushbutton
  1a = Square Pushbutton
  Start = Square Pushbutton
  R4 = Resistor [tolerance=±5% resistance=470 package="0603 [SMD]"]
  R5 = Resistor [tolerance=±5% resistance=470 package="0603 [SMD]"]
  1000uF_25V = Capacitor Polarized [package=panasonic_g]
  1000uF_25V_2 = Capacitor Polarized [package=panasonic_g]
  4b = Square Pushbutton
  part = Arduino Micro (Rev3)

nets:
  N1: Lestrip_warmwit.DIn, R4.Pin_1
  VCC: Lestrip_warmwit.VCC, Ledstrip_RGB.VCC, 1000uF_25V.+, 1000uF_25V_2.+
  0V: Lestrip_warmwit.VSS, 4a.leg1, 3b.leg1, 3a.leg1, 2b.leg1, 2a.leg1, 1b.leg1, 1a.leg1, Start.leg1, 1000uF_25V_2.-, 4b.leg1, part.GND
  N2: Ledstrip_RGB.DIn, R5.Pin_1
  N3: Ledstrip_RGB.VSS, 1000uF_25V.-
  N4: 4a.leg0, part.D5_PWM
  N5: 3b.leg0, part.D6_PWM/A7
  N6: 3a.leg0, part.D7
  N7: 2b.leg0, part.D8_PWM/A8
  N8: 2a.leg0, part.D9_PWM/A9
  N9: 1b.leg0, part.D10_PWM/A10
  N10: 1a.leg0, part.D11_PWM
  N11: Start.leg0, part.D13_PWM
  N12: R5.Pin_0, part.A0
  N13: 4b.leg0, part.D4_PWM/A6
