# Fritzing sketch 47b-KikkerkokenOutput (saved by Fritzing 1.0.6)
breadboards: 1

parts:
  Laag_4 = SMD RGB LED (WS2812) [package=5050]
  Laag_3 = SMD RGB LED (WS2812) [package=5050]
  Nano1 = Arduino Nano (Rev3.0)
  7 = Square Pushbutton
  5 = Square Pushbutton  # not connected
  4 = Square Pushbutton  # not connected
  6 = Square Pushbutton  # not connected
  0 = Square Pushbutton  # not connected
  1 = Square Pushbutton  # not connected
  2 = Square Pushbutton  # not connected
  4_2 = Square Pushbutton  # not connected
  R8 = Resistor [tolerance=±5% resistance=470 package="0603 [SMD]"]
  R9 = Resistor [tolerance=±5% resistance=470 package="0603 [SMD]"]
  C3 = Capacitor Polarized [package=panasonic_g]
  C4 = Capacitor Polarized [package=panasonic_g]
  Laag_2 = SMD RGB LED (WS2812) [package=5050]
  Laag_1 = SMD RGB LED (WS2812) [package=5050]
  R10 = Resistor [tolerance=±5% resistance=470 package="0603 [SMD]"]
  R11 = Resistor [tolerance=±5% resistance=470 package="0603 [SMD]"]
  MP3_module = TRRS 3.5mm Jack Breakout
  C5 = Capacitor Polarized [package=panasonic_g]
  C6 = Capacitor Polarized [package=panasonic_g]

nets:
  N1: Laag_4.DIn, R9.Pin_1
  5V: Laag_4.VCC, Laag_3.VCC, Nano1.5V, C3.+, C4.+, Laag_2.VCC, Laag_1.VCC, MP3_module.TIP, C5.+, C6.+
  GND: Laag_4.VSS, C3.-, MP3_module.SLEEVE
  N2: Laag_3.DIn, R8.Pin_1
  VSS: Laag_3.VSS, Nano1.GND, 7.leg1, C4.-, Laag_2.VSS, Laag_1.VSS, C5.-, C6.-
  N3: Nano1.D11/MOSI, MP3_module.RING2
  N4: Nano1.D12/MISO, MP3_module.RING1
  N5: Nano1.A3, R11.Pin_0
  N6: Nano1.A2, R10.Pin_0
  N7: Nano1.A1, R8.Pin_0
  N8: Nano1.A0, R9.Pin_0
  N9: Laag_2.DIn, R10.Pin_1
  N10: Laag_1.DIn, R11.Pin_1

notes:
  Grove - MP3 v2.0
